// Logisim project PROCESSOR.circ as structural Verilog: 7 circuits, main circuit main
module main (
  input  in_1,
  input  [31:0] in_2,
  output [3:0] out_3,
  output [31:0] input_rf,
  output [31:0] OP2,
  output [1:0] out_6,
  output [15:0] out_7,
  output [31:0] OP1,
  output [4:0] ADDR_A
);

  wire and_2_out, and_3_out, and_5_out, clock_1_out, comparator_1_eq, comparator_2_eq, comparator_3_eq,
       comparator_4_eq, comparator_5_eq, comparator_6_eq, comparator_7_eq, comparator_8_eq, comparator_9_eq,
       demultiplexer_2_out0, demultiplexer_2_out1, demultiplexer_2_out2, demultiplexer_2_out3,
       demultiplexer_2_out4, demultiplexer_2_out5, demultiplexer_2_out6, demultiplexer_2_out7,
       demultiplexer_2_out8, demultiplexer_2_out9, demultiplexer_2_out10, demultiplexer_2_out11,
       demultiplexer_2_out12, demultiplexer_2_out13, demultiplexer_2_out14, demultiplexer_2_out15,
       demultiplexer_2_out16, demultiplexer_2_out17, demultiplexer_2_out18, demultiplexer_2_out19,
       demultiplexer_2_out20, demultiplexer_2_out21, demultiplexer_2_out22, demultiplexer_2_out23,
       demultiplexer_2_out24, demultiplexer_2_out25, demultiplexer_2_out26, demultiplexer_2_out27,
       demultiplexer_2_out28, demultiplexer_2_out29, demultiplexer_2_out30, demultiplexer_2_out31,
       halt_1_out_2, load_1_out_2, move_1_out_2, not_1_out, not_2_out, not_3_out, not_4_out, not_5_out,
       not_6_out, or_1_out, PC_IR_ENABLE, store_1_out_2, store_2_out_2;
  wire [2:0] COUNTER;
  wire [4:0] multiplexer_2_out;
  wire [15:0] adder_1_out, bit_extender_1_out, multiplexer_1_out, PC_q, RZ_q;
  wire [31:0] alu_1_output, bit_extender_2_out, demultiplexer_1_out0, demultiplexer_1_out1,
       multiplexer_3_out, multiplexer_4_out, multiplexer_5_out, R1_q, R2_q, R3_q, R4_q, R5_q, R6_q, R7_q,
       R8_q, R9_q, R10_q, R11_q, R12_q, R13_q, R14_q, R15_q, r16_q, R17_q, R18_q, R19_q, R20_q, R21_q, R22_q,
       R23_q, R24_q, R25_q, R26_q, r27_q, R28_q, R29_q, R30_q, R31_q, R32_q, RA_q, ram_1_data, RB_q, RM_q;
  wire [31:4] IR_q;

  HALT halt_1 (.in_1(out_3), .out_2(halt_1_out_2));
  not not_1 (not_1_out, halt_1_out_2);
  Comparator #(.width(3)) comparator_1 (.a(COUNTER), .b(3'b000), .eq(comparator_1_eq));  // open: gt, lt
  Adder #(.width(16)) adder_1 (.a(PC_q), .b(bit_extender_1_out), .out(adder_1_out));  // open: cin, cout
  assign bit_extender_1_out = {{15{1'b0}}, 1'b1};  // Bit_Extender bit_extender_1
  and and_1 (PC_IR_ENABLE, comparator_1_eq, not_1_out);
  Register #(.width(16)) PC (.D(adder_1_out), .en(PC_IR_ENABLE), .Q(PC_q), .clk(clock_1_out), .clr(in_1));
  Counter #(.width(3), .max('h7)) counter_1 (
    .Q(COUNTER), .clk(clock_1_out), .clr(or_1_out));  // open: load, D, count, carry
  not not_2 (not_2_out, COUNTER[1]);
  Comparator #(.width(3)) comparator_2 (.a(COUNTER), .b(3'b011), .eq(comparator_2_eq));  // open: gt, lt
  STORE store_1 (.in_1(out_3), .out_2(store_1_out_2));
  Comparator #(.width(3)) comparator_3 (.a(COUNTER), .b(3'b011), .eq(comparator_3_eq));  // open: gt, lt
  and and_2 (and_2_out, COUNTER[0], not_2_out, COUNTER[2]);
  Multiplexer #(.width(16)) multiplexer_1 (
    .in0(PC_q), .in1(out_7), .out(multiplexer_1_out), .sel(comparator_2_eq));  // open: en
  and and_3 (and_3_out, store_1_out_2, comparator_3_eq);
  Clock clock_1 (.out(clock_1_out));
  or or_1 (or_1_out, and_2_out, in_1);
  not not_3 (not_3_out, and_3_out);
  Comparator #(.width(3)) comparator_4 (.a(COUNTER), .b(3'b011), .eq(comparator_4_eq));  // open: gt, lt
  RAM #(.addrWidth(16), .dataWidth(32), .bus("separate")) ram_1 (
    .addr(multiplexer_1_out), .din(RM_q), .data(ram_1_data), .str(and_3_out), .clk(clock_1_out),
    .ld(not_3_out));  // open: sel, clr
  Demultiplexer #(.width(32), .enable("false")) demultiplexer_1 (
    .out0(demultiplexer_1_out0), .out1(demultiplexer_1_out1), .in(ram_1_data), .sel(comparator_4_eq));
  Register #(.width(32)) IR (
    .D(demultiplexer_1_out0), .en(PC_IR_ENABLE), .Q({IR_q[31:14], ADDR_A, IR_q[8:4], out_3}),
    .clk(clock_1_out), .clr(in_1));
  Comparator #(.width(3)) comparator_5 (.a(COUNTER), .b(3'b001), .eq(comparator_5_eq));  // open: gt, lt
  assign bit_extender_2_out = {{16{1'b0}}, IR_q[31:16]};  // Bit_Extender bit_extender_2
  STORE store_2 (.in_1(out_3), .out_2(store_2_out_2));
  not not_4 (not_4_out, out_3[1]);
  not not_5 (not_5_out, out_3[2]);
  not not_6 (not_6_out, out_3[3]);
  MOVE move_1 (.OPCODE(out_3), .out_2(move_1_out_2));
  Multiplexer #(.width(5), .enable("false")) multiplexer_2 (
    .in0(IR_q[18:14]), .in1(IR_q[8:4]), .out(multiplexer_2_out), .sel(store_2_out_2));
  and and_4 (out_6[0], not_4_out, out_3[3]);
  and and_5 (and_5_out, not_4_out, not_5_out);
  or or_2 (out_6[1], and_5_out, not_6_out);
  Register #(.width(32)) RA (.D(OP1), .en(comparator_5_eq), .Q(RA_q), .clk(clock_1_out), .clr(in_1));
  Register #(.width(32)) RB (.D(OP2), .en(comparator_5_eq), .Q(RB_q), .clk(clock_1_out), .clr(in_1));
  Multiplexer #(.width(32)) multiplexer_3 (
    .in0(RA_q), .in1(in_2), .out(multiplexer_3_out), .sel(move_1_out_2));  // open: en
  ALU alu_1 (.INPUT_1(multiplexer_3_out), .INPUT_2(multiplexer_4_out), .ALU_SELECT(out_6), .OUTPUT(alu_1_output));
  LOAD load_1 (.in_1(out_3), .out_2(load_1_out_2));
  Comparator #(.width(3)) comparator_6 (.a(COUNTER), .b(3'b010), .eq(comparator_6_eq));  // open: gt, lt
  Multiplexer #(.width(32)) multiplexer_4 (
    .in0(RB_q), .in1(bit_extender_2_out), .out(multiplexer_4_out), .sel(out_3[0]));  // open: en
  Register #(.width(32)) RZ (.D(alu_1_output), .en(comparator_6_eq), .Q({RZ_q, out_7}), .clk(clock_1_out), .clr(in_1));
  Register #(.width(32)) RM (.D(RB_q), .en(comparator_7_eq), .Q(RM_q), .clk(clock_1_out), .clr(in_1));
  Multiplexer #(.width(32)) multiplexer_5 (
    .in0({RZ_q, out_7}), .in1(demultiplexer_1_out1), .out(multiplexer_5_out), .sel(load_1_out_2));  // open: en
  Comparator #(.width(3)) comparator_7 (.a(COUNTER), .b(3'b010), .eq(comparator_7_eq));  // open: gt, lt
  Comparator #(.width(3)) comparator_8 (.a(COUNTER), .b(3'b011), .eq(comparator_8_eq));  // open: gt, lt
  Register #(.width(32)) RY (.D(multiplexer_5_out), .en(comparator_8_eq), .Q(input_rf), .clk(clock_1_out), .clr(in_1));
  Comparator #(.width(3)) comparator_9 (.a(COUNTER), .b(3'b100), .eq(comparator_9_eq));  // open: gt, lt
  Demultiplexer #(.select(5)) demultiplexer_2 (
    .out0(demultiplexer_2_out0), .out1(demultiplexer_2_out1), .out2(demultiplexer_2_out2),
    .out3(demultiplexer_2_out3), .out4(demultiplexer_2_out4), .out5(demultiplexer_2_out5),
    .out6(demultiplexer_2_out6), .out7(demultiplexer_2_out7), .out8(demultiplexer_2_out8),
    .out9(demultiplexer_2_out9), .out10(demultiplexer_2_out10), .out11(demultiplexer_2_out11),
    .out12(demultiplexer_2_out12), .out13(demultiplexer_2_out13), .out14(demultiplexer_2_out14),
    .out15(demultiplexer_2_out15), .out16(demultiplexer_2_out16), .out17(demultiplexer_2_out17),
    .out18(demultiplexer_2_out18), .out19(demultiplexer_2_out19), .out20(demultiplexer_2_out20),
    .out21(demultiplexer_2_out21), .out22(demultiplexer_2_out22), .out23(demultiplexer_2_out23),
    .out24(demultiplexer_2_out24), .out25(demultiplexer_2_out25), .out26(demultiplexer_2_out26),
    .out27(demultiplexer_2_out27), .out28(demultiplexer_2_out28), .out29(demultiplexer_2_out29),
    .out30(demultiplexer_2_out30), .out31(demultiplexer_2_out31), .in(comparator_9_eq), .sel(IR_q[8:4]));  // open: en
  Register #(.width(32)) R1 (.D(input_rf), .en(demultiplexer_2_out0), .Q(R1_q), .clk(clock_1_out));  // open: clr
  Register #(.width(32)) R2 (.D(input_rf), .en(demultiplexer_2_out1), .Q(R2_q), .clk(clock_1_out));  // open: clr
  Register #(.width(32)) R3 (.D(input_rf), .en(demultiplexer_2_out2), .Q(R3_q), .clk(clock_1_out));  // open: clr
  Register #(.width(32)) R4 (.D(input_rf), .en(demultiplexer_2_out3), .Q(R4_q), .clk(clock_1_out));  // open: clr
  Register #(.width(32)) R5 (.D(input_rf), .en(demultiplexer_2_out4), .Q(R5_q), .clk(clock_1_out));  // open: clr
  Register #(.width(32)) R6 (.D(input_rf), .en(demultiplexer_2_out5), .Q(R6_q), .clk(clock_1_out));  // open: clr
  Register #(.width(32)) R7 (.D(input_rf), .en(demultiplexer_2_out6), .Q(R7_q), .clk(clock_1_out));  // open: clr
  Register #(.width(32)) R8 (.D(input_rf), .en(demultiplexer_2_out7), .Q(R8_q), .clk(clock_1_out));  // open: clr
  Register #(.width(32)) R9 (.D(input_rf), .en(demultiplexer_2_out8), .Q(R9_q), .clk(clock_1_out));  // open: clr
  Register #(.width(32)) R10 (.D(input_rf), .en(demultiplexer_2_out9), .Q(R10_q), .clk(clock_1_out));  // open: clr
  Register #(.width(32)) R12 (.D(input_rf), .en(demultiplexer_2_out11), .Q(R12_q), .clk(clock_1_out));  // open: clr
  Register #(.width(32)) R13 (.D(input_rf), .en(demultiplexer_2_out12), .Q(R13_q), .clk(clock_1_out));  // open: clr
  Register #(.width(32)) R14 (.D(input_rf), .en(demultiplexer_2_out13), .Q(R14_q), .clk(clock_1_out));  // open: clr
  Register #(.width(32)) R15 (.D(input_rf), .en(demultiplexer_2_out14), .Q(R15_q), .clk(clock_1_out));  // open: clr
  Register #(.width(32)) r16 (.D(input_rf), .en(demultiplexer_2_out15), .Q(r16_q), .clk(clock_1_out));  // open: clr
  Register #(.width(32)) R11 (.D(input_rf), .en(demultiplexer_2_out10), .Q(R11_q), .clk(clock_1_out));  // open: clr
  Register #(.width(32)) R17 (.D(input_rf), .en(demultiplexer_2_out16), .Q(R17_q), .clk(clock_1_out));  // open: clr
  Register #(.width(32)) R18 (.D(input_rf), .en(demultiplexer_2_out17), .Q(R18_q), .clk(clock_1_out));  // open: clr
  Register #(.width(32)) R19 (.D(input_rf), .en(demultiplexer_2_out18), .Q(R19_q), .clk(clock_1_out));  // open: clr
  Register #(.width(32)) R20 (.D(input_rf), .en(demultiplexer_2_out19), .Q(R20_q), .clk(clock_1_out));  // open: clr
  Register #(.width(32)) R21 (.D(input_rf), .en(demultiplexer_2_out20), .Q(R21_q), .clk(clock_1_out));  // open: clr
  Register #(.width(32)) R22 (.D(input_rf), .en(demultiplexer_2_out21), .Q(R22_q), .clk(clock_1_out));  // open: clr
  Register #(.width(32)) R23 (.D(input_rf), .en(demultiplexer_2_out22), .Q(R23_q), .clk(clock_1_out));  // open: clr
  Register #(.width(32)) R24 (.D(input_rf), .en(demultiplexer_2_out23), .Q(R24_q), .clk(clock_1_out));  // open: clr
  Register #(.width(32)) R25 (.D(input_rf), .en(demultiplexer_2_out24), .Q(R25_q), .clk(clock_1_out));  // open: clr
  Register #(.width(32)) R26 (.D(input_rf), .en(demultiplexer_2_out25), .Q(R26_q), .clk(clock_1_out));  // open: clr
  Register #(.width(32)) r27 (.D(input_rf), .en(demultiplexer_2_out26), .Q(r27_q), .clk(clock_1_out));  // open: clr
  Register #(.width(32)) R28 (.D(input_rf), .en(demultiplexer_2_out27), .Q(R28_q), .clk(clock_1_out));  // open: clr
  Register #(.width(32)) R30 (.D(input_rf), .en(demultiplexer_2_out29), .Q(R30_q), .clk(clock_1_out));  // open: clr
  Register #(.width(32)) R31 (.D(input_rf), .en(demultiplexer_2_out30), .Q(R31_q), .clk(clock_1_out));  // open: clr
  Register #(.width(32)) R32 (.D(input_rf), .en(demultiplexer_2_out31), .Q(R32_q), .clk(clock_1_out));  // open: clr
  Register #(.width(32)) R29 (.D(input_rf), .en(demultiplexer_2_out28), .Q(R29_q), .clk(clock_1_out));  // open: clr
  Multiplexer #(.select(5), .width(32)) multiplexer_6 (
    .in0(R1_q), .in1(R2_q), .in2(R3_q), .in3(R4_q), .in4(R5_q), .in5(R6_q), .in6(R7_q), .in7(R8_q),
    .in8(R9_q), .in9(R10_q), .in10(R11_q), .in11(R12_q), .in12(R13_q), .in13(R14_q), .in14(R15_q),
    .in15(r16_q), .in16(R17_q), .in17(R18_q), .in18(R19_q), .in19(R20_q), .in20(R21_q), .in21(R22_q),
    .in22(R23_q), .in23(R24_q), .in24(R25_q), .in25(R26_q), .in26(r27_q), .in27(R28_q), .in28(R29_q),
    .in29(R30_q), .in30(R31_q), .in31(R32_q), .out(OP2), .sel(multiplexer_2_out));  // open: en
  Multiplexer #(.select(5), .width(32)) multiplexer_7 (
    .in0(R1_q), .in1(R2_q), .in2(R3_q), .in3(R4_q), .in4(R5_q), .in5(R6_q), .in6(R7_q), .in7(R8_q),
    .in8(R9_q), .in9(R10_q), .in10(R11_q), .in11(R12_q), .in12(R13_q), .in13(R14_q), .in14(R15_q),
    .in15(r16_q), .in16(R17_q), .in17(R18_q), .in18(R19_q), .in19(R20_q), .in20(R21_q), .in21(R22_q),
    .in22(R23_q), .in23(R24_q), .in24(R25_q), .in25(R26_q), .in26(r27_q), .in27(R28_q), .in28(R29_q),
    .in29(R30_q), .in30(R31_q), .in31(R32_q), .out(OP1), .sel(ADDR_A));  // open: en

  // Other names for the same wires on the sheet: RESET_PC = in_1
endmodule

module ALU (
  input  [31:0] INPUT_1,
  input  [31:0] INPUT_2,
  input  [1:0] ALU_SELECT,
  output [31:0] OUTPUT
);

  wire [31:0] adder_1_out, and_1_out, or_1_out, subtractor_1_out;

  assign and_1_out = INPUT_1 & INPUT_2;  // AND_Gate and_1, 32 bits wide
  assign or_1_out = INPUT_1 | INPUT_2;  // OR_Gate or_1, 32 bits wide
  Subtractor #(.width(32)) subtractor_1 (.a(INPUT_1), .b(INPUT_2), .out(subtractor_1_out));  // open: bin, bout
  Adder #(.width(32)) adder_1 (.a(INPUT_1), .b(INPUT_2), .out(adder_1_out));  // open: cin, cout
  Multiplexer #(.select(2), .width(32)) multiplexer_1 (
    .in0(and_1_out), .in1(or_1_out), .in2(adder_1_out), .in3(subtractor_1_out), .out(OUTPUT), .sel(ALU_SELECT));  // open: en
endmodule

module REGFILE (
  input  [31:0] INPUT_RF,
  input  in_2,
  input  [4:0] ADDRESS_B,
  input  [4:0] ADDRESS_C,
  input  [4:0] ADDRESS_A,
  output [31:0] OP2,
  output [31:0] OP1
);

  wire clock_1_out, demultiplexer_1_out0, demultiplexer_1_out1, demultiplexer_1_out2, demultiplexer_1_out3,
       demultiplexer_1_out4, demultiplexer_1_out5, demultiplexer_1_out6, demultiplexer_1_out7,
       demultiplexer_1_out8, demultiplexer_1_out9, demultiplexer_1_out10, demultiplexer_1_out11,
       demultiplexer_1_out12, demultiplexer_1_out13, demultiplexer_1_out14, demultiplexer_1_out15,
       demultiplexer_1_out16, demultiplexer_1_out17, demultiplexer_1_out18, demultiplexer_1_out19,
       demultiplexer_1_out20, demultiplexer_1_out21, demultiplexer_1_out22, demultiplexer_1_out23,
       demultiplexer_1_out24, demultiplexer_1_out25, demultiplexer_1_out26, demultiplexer_1_out27,
       demultiplexer_1_out28, demultiplexer_1_out29, demultiplexer_1_out30, demultiplexer_1_out31;
  wire [31:0] R1_q, R2_q, R3_q, R4_q, R5_q, R6_q, R7_q, R8_q, R9_q, R10_q, R11_q, R12_q, R13_q, R14_q, R15_q,
       r16_q, R17_q, R18_q, R19_q, R20_q, R21_q, R22_q, R23_q, R24_q, R25_q, R26_q, r27_q, R28_q, R29_q,
       R30_q, R31_q, R32_q;

  Clock clock_1 (.out(clock_1_out));
  Demultiplexer #(.select(5)) demultiplexer_1 (
    .out0(demultiplexer_1_out0), .out1(demultiplexer_1_out1), .out2(demultiplexer_1_out2),
    .out3(demultiplexer_1_out3), .out4(demultiplexer_1_out4), .out5(demultiplexer_1_out5),
    .out6(demultiplexer_1_out6), .out7(demultiplexer_1_out7), .out8(demultiplexer_1_out8),
    .out9(demultiplexer_1_out9), .out10(demultiplexer_1_out10), .out11(demultiplexer_1_out11),
    .out12(demultiplexer_1_out12), .out13(demultiplexer_1_out13), .out14(demultiplexer_1_out14),
    .out15(demultiplexer_1_out15), .out16(demultiplexer_1_out16), .out17(demultiplexer_1_out17),
    .out18(demultiplexer_1_out18), .out19(demultiplexer_1_out19), .out20(demultiplexer_1_out20),
    .out21(demultiplexer_1_out21), .out22(demultiplexer_1_out22), .out23(demultiplexer_1_out23),
    .out24(demultiplexer_1_out24), .out25(demultiplexer_1_out25), .out26(demultiplexer_1_out26),
    .out27(demultiplexer_1_out27), .out28(demultiplexer_1_out28), .out29(demultiplexer_1_out29),
    .out30(demultiplexer_1_out30), .out31(demultiplexer_1_out31), .in(in_2), .sel(ADDRESS_C));  // open: en
  Register #(.width(32)) R1 (.D(INPUT_RF), .en(demultiplexer_1_out0), .Q(R1_q), .clk(clock_1_out));  // open: clr
  Register #(.width(32)) R2 (.D(INPUT_RF), .en(demultiplexer_1_out1), .Q(R2_q), .clk(clock_1_out));  // open: clr
  Register #(.width(32)) R3 (.D(INPUT_RF), .en(demultiplexer_1_out2), .Q(R3_q), .clk(clock_1_out));  // open: clr
  Register #(.width(32)) R4 (.D(INPUT_RF), .en(demultiplexer_1_out3), .Q(R4_q), .clk(clock_1_out));  // open: clr
  Register #(.width(32)) R5 (.D(INPUT_RF), .en(demultiplexer_1_out4), .Q(R5_q), .clk(clock_1_out));  // open: clr
  Register #(.width(32)) R6 (.D(INPUT_RF), .en(demultiplexer_1_out5), .Q(R6_q), .clk(clock_1_out));  // open: clr
  Register #(.width(32)) R7 (.D(INPUT_RF), .en(demultiplexer_1_out6), .Q(R7_q), .clk(clock_1_out));  // open: clr
  Register #(.width(32)) R8 (.D(INPUT_RF), .en(demultiplexer_1_out7), .Q(R8_q), .clk(clock_1_out));  // open: clr
  Register #(.width(32)) R9 (.D(INPUT_RF), .en(demultiplexer_1_out8), .Q(R9_q), .clk(clock_1_out));  // open: clr
  Register #(.width(32)) R10 (.D(INPUT_RF), .en(demultiplexer_1_out9), .Q(R10_q), .clk(clock_1_out));  // open: clr
  Register #(.width(32)) R11 (.D(INPUT_RF), .en(demultiplexer_1_out10), .Q(R11_q), .clk(clock_1_out));  // open: clr
  Register #(.width(32)) R12 (.D(INPUT_RF), .en(demultiplexer_1_out11), .Q(R12_q), .clk(clock_1_out));  // open: clr
  Register #(.width(32)) R13 (.D(INPUT_RF), .en(demultiplexer_1_out12), .Q(R13_q), .clk(clock_1_out));  // open: clr
  Register #(.width(32)) R14 (.D(INPUT_RF), .en(demultiplexer_1_out13), .Q(R14_q), .clk(clock_1_out));  // open: clr
  Register #(.width(32)) R15 (.D(INPUT_RF), .en(demultiplexer_1_out14), .Q(R15_q), .clk(clock_1_out));  // open: clr
  Register #(.width(32)) r16 (.D(INPUT_RF), .en(demultiplexer_1_out15), .Q(r16_q), .clk(clock_1_out));  // open: clr
  Register #(.width(32)) R17 (.D(INPUT_RF), .en(demultiplexer_1_out16), .Q(R17_q), .clk(clock_1_out));  // open: clr
  Register #(.width(32)) R18 (.D(INPUT_RF), .en(demultiplexer_1_out17), .Q(R18_q), .clk(clock_1_out));  // open: clr
  Register #(.width(32)) R19 (.D(INPUT_RF), .en(demultiplexer_1_out18), .Q(R19_q), .clk(clock_1_out));  // open: clr
  Register #(.width(32)) R20 (.D(INPUT_RF), .en(demultiplexer_1_out19), .Q(R20_q), .clk(clock_1_out));  // open: clr
  Register #(.width(32)) R21 (.D(INPUT_RF), .en(demultiplexer_1_out20), .Q(R21_q), .clk(clock_1_out));  // open: clr
  Register #(.width(32)) R22 (.D(INPUT_RF), .en(demultiplexer_1_out21), .Q(R22_q), .clk(clock_1_out));  // open: clr
  Register #(.width(32)) R23 (.D(INPUT_RF), .en(demultiplexer_1_out22), .Q(R23_q), .clk(clock_1_out));  // open: clr
  Register #(.width(32)) R24 (.D(INPUT_RF), .en(demultiplexer_1_out23), .Q(R24_q), .clk(clock_1_out));  // open: clr
  Register #(.width(32)) r27 (.D(INPUT_RF), .en(demultiplexer_1_out26), .Q(r27_q), .clk(clock_1_out));  // open: clr
  Register #(.width(32)) R25 (.D(INPUT_RF), .en(demultiplexer_1_out24), .Q(R25_q), .clk(clock_1_out));  // open: clr
  Register #(.width(32)) R26 (.D(INPUT_RF), .en(demultiplexer_1_out25), .Q(R26_q), .clk(clock_1_out));  // open: clr
  Register #(.width(32)) R28 (.D(INPUT_RF), .en(demultiplexer_1_out27), .Q(R28_q), .clk(clock_1_out));  // open: clr
  Register #(.width(32)) R29 (.D(INPUT_RF), .en(demultiplexer_1_out28), .Q(R29_q), .clk(clock_1_out));  // open: clr
  Register #(.width(32)) R30 (.D(INPUT_RF), .en(demultiplexer_1_out29), .Q(R30_q), .clk(clock_1_out));  // open: clr
  Register #(.width(32)) R31 (.D(INPUT_RF), .en(demultiplexer_1_out30), .Q(R31_q), .clk(clock_1_out));  // open: clr
  Register #(.width(32)) R32 (.D(INPUT_RF), .en(demultiplexer_1_out31), .Q(R32_q), .clk(clock_1_out));  // open: clr
  Multiplexer #(.select(5), .width(32)) multiplexer_1 (
    .in0(R1_q), .in1(R2_q), .in2(R3_q), .in3(R4_q), .in4(R5_q), .in5(R6_q), .in6(R7_q), .in7(R8_q),
    .in8(R9_q), .in9(R10_q), .in10(R11_q), .in11(R12_q), .in12(R13_q), .in13(R14_q), .in14(R15_q),
    .in15(r16_q), .in16(R17_q), .in17(R18_q), .in18(R19_q), .in19(R20_q), .in20(R21_q), .in21(R22_q),
    .in22(R23_q), .in23(R24_q), .in24(R25_q), .in25(R26_q), .in26(r27_q), .in27(R28_q), .in28(R29_q),
    .in29(R30_q), .in30(R31_q), .in31(R32_q), .out(OP2), .sel(ADDRESS_B));  // open: en
  Multiplexer #(.select(5), .width(32)) multiplexer_2 (
    .in0(R1_q), .in1(R2_q), .in2(R3_q), .in3(R4_q), .in4(R5_q), .in5(R6_q), .in6(R7_q), .in7(R8_q),
    .in8(R9_q), .in9(R10_q), .in10(R11_q), .in11(R12_q), .in12(R13_q), .in13(R14_q), .in14(R15_q),
    .in15(r16_q), .in16(R17_q), .in17(R18_q), .in18(R19_q), .in19(R20_q), .in20(R21_q), .in21(R22_q),
    .in22(R23_q), .in23(R24_q), .in24(R25_q), .in25(R26_q), .in26(r27_q), .in27(R28_q), .in28(R29_q),
    .in29(R30_q), .in30(R31_q), .in31(R32_q), .out(OP1), .sel(ADDRESS_A));  // open: en
endmodule

module HALT (
  input  [3:0] in_1,
  output out_2
);

  wire not_1_out;

  not not_1 (not_1_out, in_1[0]);
  and and_1 (out_2, not_1_out, in_1[1], in_1[2], in_1[3]);
endmodule

module LOAD (
  input  [3:0] in_1,
  output out_2
);

  wire not_1_out, not_2_out;

  not not_1 (not_1_out, in_1[3]);
  not not_2 (not_2_out, in_1[2]);
  and and_1 (out_2, not_1_out, not_2_out, in_1[1], in_1[0]);
endmodule

module STORE (
  input  [3:0] in_1,
  output out_2
);

  wire not_1_out, not_2_out;

  not not_1 (not_1_out, in_1[3]);
  not not_2 (not_2_out, in_1[1]);
  and and_1 (out_2, not_2_out, in_1[0], not_1_out, in_1[2]);
endmodule

module MOVE (
  input  [3:0] OPCODE,
  output out_2
);

  wire not_1_out, not_2_out, not_3_out, not_4_out;

  not not_1 (not_1_out, OPCODE[0]);
  not not_2 (not_2_out, OPCODE[1]);
  not not_3 (not_3_out, OPCODE[2]);
  not not_4 (not_4_out, OPCODE[3]);
  nor nor_1 (out_2, OPCODE[3], OPCODE[1], OPCODE[2]);
endmodule
